# Fritzing sketch schematics (saved by Fritzing 0.9.3b)
breadboards: 1

parts:
  Composant1 = Arduino Pro Mini (3.3V)
  M1 = DC Motor
  L298N1 = L298N DC motor driver
  BAT1 = 12 battery [package=battery]
  S1 = SPST Slide Switch [package="SIP THT"]
  S2 = SPST Slide Switch [package="SIP THT"]
  Mod1 = KY-018 Photoresistor Module [package="Breakout board"]

nets:
  N1: Composant1.RAW, L298N1.5V#7
  GND: Composant1.GND, L298N1.GND, BAT1.-, S1.L2, S2.L2, Mod1.Vin
  N2: Composant1.A3, Mod1.S
  N3: Composant1.SCK, Mod1.-
  N4: Composant1.D8, L298N1.IN2
  N5: Composant1.D7, L298N1.IN1
  N6: Composant1.D3, S2.L1
  N7: Composant1.D2, S1.L1
  N8: M1.pin_1, L298N1.OUT2
  N9: M1.pin_2, L298N1.OUT1
  N10: L298N1.12V, BAT1.+
  N11: L298N1.5V#9, L298N1.ENA

notes:
  Top switch
  Bottom switch
  12V 2.8Ah battery
  L298N driver board
  12V 35rpm DC motor
  Photocell
  Arduino Pro Mini 3.3V

custom parts:
  L298N DC motor driver: 2x DC motor driver with 78M05 positive voltage regulator (7..35 V) L298N: max 46 V, 2 A Set 5 V Enable jumper to enable 5 V regultor (needed for the L298N) and +5 V output at screw terminal or supply external +5 V at screw terminal Set ENA and/or ENB to +5 V to enable motor permanently or supply ENA and/or ENB with PWM signal IN1 and IN2 set rotation directory for motor A (OUT1/OUT2) IN2 and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
  12 battery: 12V lead acid type battery, like the Husqvarna YTH2448 12V 35AH battery. This is the mini version 1/4 the size of the actual battery to be closer to typical breadboard parts (around 2in wide rathher than 7in). The pads in pcb are sized to accomidate up to 14ga wire (as these batterys will deliver high currents.)
  SPST Slide Switch: SPST slide switch with inline 100mil spacing through hole connection terminals
  KY-018 Photoresistor Module: KY-018 Photoresistor module, used to measure light intensity. It can determine the presence or absence of light.
